# Fritzing sketch Timers_wiring (saved by Fritzing 0.9.5d)

parts:
  RE2 = KY-040 Rotary encoder [package=THT]
  Part2 = Adafruit Datalogger Shield v1 [part_number="Adafruit #1141"]
  LCD2004-I2C1 = LCD2004-I2C
  M1 = >Wemos D1 R32
  M2 = omron relay module 8way
  DHT1 = DHT11 Humitidy and Temperature Sensor
  R1 = Resistor [tolerance=±5% resistance=10k package="0402 [SMD]"]
  R2 = Resistor [tolerance=±5% resistance=330 package="0402 [SMD]"]

nets:
  GND: RE2.GND, Part2.GND, LCD2004-I2C1.GND
  VCC: RE2.Vcc, Part2.3.3V
  N1: RE2.SW, Part2.D5
  N2: RE2.DT, Part2.D6
  N3: RE2.CLK, Part2.D7
  N4: Part2.SCL, LCD2004-I2C1.SCL
  N5: Part2.SDA, LCD2004-I2C1.SDA
  +5V: Part2.+5V, LCD2004-I2C1.VCC
  3V3: M1.3V3, DHT1.VDD, R2.Pin_0
  N6: M1.5V, M2.DC+
  GND_2: M1.GND, M2.DC-, DHT1.GND
  N7: M1.IO2, M2.CH1
  N8: M1.IO4, M2.CH2
  N9: M1.IO26, M2.CH7
  N10: M1.IO25, M2.CH6
  N11: M1.IO12, M2.CH3
  N12: M1.IO13, M2.CH4
  N13: M1.IO15, DHT1.DATA, R1.Pin_1
  N14: M1.IO33, M2.CH5
  N15: M1.IO32, M2.CH8

notes:
  since the old data logging sheld connect the pin 4 & 5 to SDA & SCL pin, remember to cut off pin 4 & 5 from SDA & SCL wire if you plan to use GPIO 39 & 39
  Addition sensor
  pin 17 (In/Out)
  35, 34, 36, 39 (In)
  are free in this schematic
  you only need to soder
  15,33,32 pin, other pin can be solder direct into logging sheild
  this under that -->
  Your load here
  this resistor is needed to keep the wifi connection stable

custom parts:
  KY-040 Rotary encoder: KY-040 Rotary Encoder with switch on breakout borad from AZ Delivery
  Adafruit Datalogger Shield v1: Here's a handy Arduino shield: we've had a lot of people looking for a dedicated and well-designed data logging shield. We worked hard to engineer an inexpensive but well-rounded design. Not only is it easy to assemble and customize, it also comes with great documentation and libraries. New! we now are carrying an 'assembled' version of this shield, with all the components pre-soldered. NOTE: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
  LCD2004-I2C: A standard character display with 4x20 characters. Comes in many colors with LCM2004 IIC attached.
  >Wemos D1 R32: Wemos D1 R32 - This board is used with dual-mode Wi-Fi and Bluetooth chips, which is safe, reliable, and scalable to a variety of applications. DC in 5V-12V, 1 analog input(3.2V max input), a Micro USB connection, Compatible with D1 R32=WiFi+bluetooth+UNO
  omron relay module 8way: Low Level 5V 8 Channel Solid State Relay Module SSR G3MB-202P 240V 2A Output with Resistive Fuse.
  DHT11 Humitidy and Temperature Sensor: DHT11 Humidity and Temperature Sensor
